// Logisim project 3_lb.circ as structural Verilog
module _1_task (
  input  in_1,
  input  [7:0] in_2,
  input  [7:0] in_3,
  output [7:0] out_4,
  output out_5
);

  Adder adder_1 (.a(in_2), .b(in_3), .out(out_4), .cin(in_1), .cout(out_5));
endmodule

module _2_task (
  input  \_1_е_слагаемое ,
  input  \_2_е_слагаемое ,
  output \Сумма_разряда ,
  output out_4
);

  wire not_1_out, or_1_out;

  or or_1 (or_1_out, \_1_е_слагаемое , \_2_е_слагаемое );
  and and_1 (out_4, \_1_е_слагаемое , \_2_е_слагаемое );
  not not_1 (not_1_out, out_4);
  and and_2 (\Сумма_разряда , or_1_out, not_1_out);

  // Notes on the sheet:
  //   Перенос на селдующий разряд
endmodule

module _3_task (
  input  cin,
  input  \_1_е_слагаемое ,
  input  \_2_е_слагаемое ,
  output \сумма ,
  output \остаток 
);

  wire and_1_out, and_2_out, not_1_out, or_1_out, or_2_out;

  not not_1 (not_1_out, or_1_out);
  or or_1 (or_1_out, \_1_е_слагаемое , \_2_е_слагаемое );
  and and_1 (and_1_out, \_1_е_слагаемое , \_2_е_слагаемое );
  not not_2 (\сумма , or_2_out);
  or or_2 (or_2_out, cin, not_1_out);
  and and_2 (and_2_out, cin, not_1_out);
  or or_3 (\остаток , and_2_out, and_1_out);
endmodule

module _4_task (
  input  [7:0] in_1,
  input  [7:0] in_2,
  input  in_3,
  output [7:0] \сумма 
);

  wire and_1_out, and_2_out, and_3_out, and_4_out, and_5_out, and_6_out, and_7_out, and_8_out, and_9_out,
       and_10_out, and_11_out, and_12_out, and_13_out, and_14_out, and_15_out, and_16_out, and_17_out,
       and_18_out, and_19_out, and_20_out, and_21_out, and_22_out, and_23_out, and_24_out, not_1_out,
       not_2_out, not_3_out, not_4_out, not_5_out, not_6_out, not_7_out, not_8_out, not_9_out, not_10_out,
       not_11_out, not_12_out, not_13_out, not_14_out, not_15_out, not_16_out, or_1_out, or_2_out, or_3_out,
       or_4_out, or_5_out, or_6_out, or_7_out, or_8_out, or_9_out, or_10_out, or_11_out, or_12_out,
       or_13_out, or_14_out, or_15_out, or_16_out, or_17_out, or_18_out, or_19_out, or_20_out, or_21_out,
       or_22_out, or_23_out, or_24_out;

  // Probe on in_2
  // Probe on in_1
  or or_1 (or_1_out, in_1[0], in_2[0]);
  and and_1 (and_1_out, in_1[0], in_2[0]);
  or or_2 (or_2_out, in_1[1], in_2[1]);
  and and_2 (and_2_out, in_1[1], in_2[1]);
  or or_3 (or_3_out, in_1[2], in_2[2]);
  and and_3 (and_3_out, in_1[2], in_2[2]);
  or or_4 (or_4_out, in_1[3], in_2[3]);
  and and_4 (and_4_out, in_1[3], in_2[3]);
  or or_5 (or_5_out, in_1[4], in_2[4]);
  and and_5 (and_5_out, in_1[4], in_2[4]);
  or or_6 (or_6_out, in_1[5], in_2[5]);
  and and_6 (and_6_out, in_1[5], in_2[5]);
  or or_7 (or_7_out, in_1[6], in_2[6]);
  and and_7 (and_7_out, in_1[6], in_2[6]);
  or or_8 (or_8_out, in_1[7], in_2[7]);
  and and_8 (and_8_out, in_1[7], in_2[7]);
  not not_1 (not_1_out, and_1_out);
  not not_2 (not_2_out, and_2_out);
  not not_3 (not_3_out, and_3_out);
  not not_4 (not_4_out, and_4_out);
  not not_5 (not_5_out, and_5_out);
  not not_6 (not_6_out, and_6_out);
  not not_7 (not_7_out, and_7_out);
  not not_8 (not_8_out, and_8_out);
  and and_9 (and_9_out, or_1_out, not_1_out);
  and and_10 (and_10_out, or_2_out, not_2_out);
  and and_11 (and_11_out, or_3_out, not_3_out);
  and and_12 (and_12_out, or_4_out, not_4_out);
  and and_13 (and_13_out, or_5_out, not_5_out);
  and and_14 (and_14_out, or_6_out, not_6_out);
  and and_15 (and_15_out, or_7_out, not_7_out);
  and and_16 (and_16_out, or_8_out, not_8_out);
  or or_9 (or_9_out, and_9_out, in_3);
  and and_17 (and_17_out, and_9_out, in_3);
  or or_10 (or_10_out, and_10_out, or_17_out);
  and and_18 (and_18_out, and_10_out, or_17_out);
  or or_11 (or_11_out, and_11_out, or_18_out);
  and and_19 (and_19_out, and_11_out, or_18_out);
  or or_12 (or_12_out, and_12_out, or_19_out);
  and and_20 (and_20_out, and_12_out, or_19_out);
  or or_13 (or_13_out, and_13_out, or_20_out);
  and and_21 (and_21_out, and_13_out, or_20_out);
  or or_14 (or_14_out, and_14_out, or_21_out);
  and and_22 (and_22_out, and_14_out, or_21_out);
  or or_15 (or_15_out, and_15_out, or_22_out);
  and and_23 (and_23_out, and_15_out, or_22_out);
  or or_16 (or_16_out, and_16_out, or_23_out);
  and and_24 (and_24_out, and_16_out, or_23_out);
  not not_9 (not_9_out, and_17_out);
  not not_10 (not_10_out, and_18_out);
  not not_11 (not_11_out, and_19_out);
  not not_12 (not_12_out, and_20_out);
  not not_13 (not_13_out, and_21_out);
  not not_14 (not_14_out, and_22_out);
  not not_15 (not_15_out, and_23_out);
  not not_16 (not_16_out, and_24_out);
  and and_25 (\сумма [0], or_9_out, not_9_out);
  or or_17 (or_17_out, and_1_out, and_17_out);
  and and_26 (\сумма [1], or_10_out, not_10_out);
  or or_18 (or_18_out, and_2_out, and_18_out);
  and and_27 (\сумма [2], or_11_out, not_11_out);
  or or_19 (or_19_out, and_3_out, and_19_out);
  and and_28 (\сумма [3], or_12_out, not_12_out);
  or or_20 (or_20_out, and_4_out, and_20_out);
  and and_29 (\сумма [4], or_13_out, not_13_out);
  or or_21 (or_21_out, and_5_out, and_21_out);
  and and_30 (\сумма [5], or_14_out, not_14_out);
  or or_22 (or_22_out, and_6_out, and_22_out);
  and and_31 (\сумма [6], or_15_out, not_15_out);
  or or_23 (or_23_out, and_7_out, and_23_out);
  and and_32 (\сумма [7], or_16_out, not_16_out);
  or or_24 (or_24_out, and_8_out, and_24_out);
  // Probe on \сумма 

  // Notes on the sheet:
  //   второе слагаемое
  //   первое слагаемое
  //   переносим остаток на следующую цепь
endmodule

module _5_task (
  input  [6:0] in_1
);

  wire button_1_out, comparator_1_eq, comparator_1_gt, comparator_1_lt, or_1_out;
  wire [6:0] keyboard_1_data;

  Keyboard keyboard_1 (.clr(button_1_out), .data(keyboard_1_data));  // open: clk, re, avail
  Button button_1 (.out(button_1_out));
  Comparator #(.width(7)) comparator_1 (
    .a(keyboard_1_data), .b(in_1), .gt(comparator_1_gt), .eq(comparator_1_eq), .lt(comparator_1_lt));
  LED led_1 (.in(comparator_1_eq));
  LED led_2 (.in(or_1_out));
  or or_1 (or_1_out, comparator_1_gt, comparator_1_lt);

  // Notes on the sheet:
  //   Очистка
  //   клавиатура
  //   код клавиши
  //   не та клавиша
  //   компаратор
  //   та клавиша
endmodule

module _6_task (
  input  \_1_е_число ,
  input  \_2_е_число ,
  output _1_2,
  output _1_2_2,
  output _2_1
);

  wire not_1_out, not_2_out, or_1_out;

  not not_1 (not_1_out, \_1_е_число );
  not not_2 (not_2_out, \_2_е_число );
  and and_1 (_1_2, \_1_е_число , not_2_out);
  or or_1 (or_1_out, _1_2, _2_1);
  and and_2 (_2_1, \_2_е_число , not_1_out);
  not not_3 (_1_2_2, or_1_out);
endmodule

module _7_task (
  input  [7:0] in_1,
  input  [7:0] in_2,
  output [7:0] a_b,
  output [7:0] a_b_2,
  output [7:0] a_b_3
);

  wire not_1_out, not_2_out, not_3_out, not_4_out, not_5_out, not_6_out, not_7_out, not_8_out, not_9_out,
       not_10_out, not_11_out, not_12_out, not_13_out, not_14_out, not_15_out, not_16_out, or_1_out,
       or_2_out, or_3_out, or_4_out, or_5_out, or_6_out, or_7_out, or_8_out;

  // Probe on in_2
  // Probe on in_1
  not not_1 (not_1_out, in_1[0]);
  not not_2 (not_2_out, in_2[0]);
  not not_3 (not_3_out, in_1[1]);
  not not_4 (not_4_out, in_2[1]);
  not not_5 (not_5_out, in_1[2]);
  not not_6 (not_6_out, in_2[2]);
  not not_7 (not_7_out, in_1[3]);
  not not_8 (not_8_out, in_2[3]);
  not not_9 (not_9_out, in_1[4]);
  not not_10 (not_10_out, in_2[4]);
  not not_11 (not_11_out, in_1[5]);
  not not_12 (not_12_out, in_2[5]);
  not not_13 (not_13_out, in_1[6]);
  not not_14 (not_14_out, in_2[6]);
  not not_15 (not_15_out, in_1[7]);
  not not_16 (not_16_out, in_2[7]);
  and and_1 (a_b_2[0], in_1[0], not_2_out);
  and and_2 (a_b_3[0], in_2[0], not_1_out);
  and and_3 (a_b_2[1], in_1[1], not_4_out);
  and and_4 (a_b_3[1], in_2[1], not_3_out);
  and and_5 (a_b_2[2], in_1[2], not_6_out);
  and and_6 (a_b_3[2], in_2[2], not_5_out);
  and and_7 (a_b_2[3], in_1[3], not_8_out);
  and and_8 (a_b_3[3], in_2[3], not_7_out);
  and and_9 (a_b_2[4], in_1[4], not_10_out);
  and and_10 (a_b_3[4], in_2[4], not_9_out);
  and and_11 (a_b_2[5], in_1[5], not_12_out);
  and and_12 (a_b_3[5], in_2[5], not_11_out);
  and and_13 (a_b_2[6], in_1[6], not_14_out);
  and and_14 (a_b_3[6], in_2[6], not_13_out);
  and and_15 (a_b_2[7], in_1[7], not_16_out);
  and and_16 (a_b_3[7], in_2[7], not_15_out);
  not not_17 (a_b[0], or_1_out);
  or or_1 (or_1_out, a_b_2[0], a_b_3[0]);
  not not_18 (a_b[1], or_2_out);
  or or_2 (or_2_out, a_b_2[1], a_b_3[1]);
  not not_19 (a_b[2], or_3_out);
  or or_3 (or_3_out, a_b_2[2], a_b_3[2]);
  not not_20 (a_b[3], or_4_out);
  or or_4 (or_4_out, a_b_2[3], a_b_3[3]);
  or or_5 (or_5_out, a_b_2[4], a_b_3[4]);
  not not_21 (a_b[4], or_5_out);
  not not_22 (a_b[5], or_6_out);
  or or_6 (or_6_out, a_b_2[5], a_b_3[5]);
  not not_23 (a_b[6], or_7_out);
  or or_7 (or_7_out, a_b_2[6], a_b_3[6]);
  or or_8 (or_8_out, a_b_2[7], a_b_3[7]);
  not not_24 (a_b[7], or_8_out);
  // Probe on a_b
  // Probe on a_b_2
  // Probe on a_b_3

  // Notes on the sheet:
  //   второе слагаемое
  //   первое слагаемое
  //   1>2
  //   1=2
  //   2>1
  //   1>2
  //   1=2
  //   2>1
  //   1>2
  //   1=2
  //   1=2
  //   2>1
  //   1>2
  //   1=2
  //   2>1
  //   1>2
  //   1=2
  //   2>1
  //   1>2
  //   1=2
  //   2>1
  //   1>2
  //   1=2
  //   2>1
endmodule
