// Logisim project task_2.circ as structural Verilog: 1 circuit, main circuit main
module main (
  input  in_1,
  input  in_2,
  input  in_3,
  output q0,
  output q1,
  output q2,
  output q3
);

  wire not_1_out, not_2_out;

  not not_1 (not_1_out, in_1);
  not not_2 (not_2_out, in_2);
  and and_1 (q0, not_1_out, in_3, not_2_out);
  and and_2 (q1, in_2, in_3, not_1_out);
  and and_3 (q2, not_2_out, in_3, in_1);
  and and_4 (q3, in_1, in_3, in_2);
endmodule
